# Fritzing sketch nodemcu-bot (saved by Fritzing 0.9.3b)
breadboards: 1

parts:
  Part2 = BME280 Breakout
  R1 = Resistor [tolerance=±5% resistance=10k package=THT]
  R2 = Resistor [tolerance=±5% resistance=10k package=THT]
  OLED_I2C1 = OLED 128x64 I2C Monochrome Display
  U1 = NodeMCU V3.0 [part_number="Lolin v0.1"]
  S1 = Toggle Switch [package=THT]
  S2 = Toggle Switch [package=THT]
  KY-1 = Keyes Relay [package=THT]
  KY-2 = Keyes Relay [package=THT]
  R3 = Resistor [tolerance=±5% resistance=10k package=THT]
  R4 = Resistor [tolerance=±5% resistance=10k package=THT]

nets:
  GND: Part2.GND, OLED_I2C1.GND, U1.GND, KY-1.ground, KY-2.ground, R3.Pin_0, R4.Pin_0
  3.3V: Part2.3.3V, R1.Pin_0, R2.Pin_0, OLED_I2C1.VDD, U1.3V3, S2.COM, KY-1.power, KY-2.power
  N1: Part2.SDI/SDA, R1.Pin_1, OLED_I2C1.SDA, U1.D2
  N2: Part2.SCK/SCL, R2.Pin_1, OLED_I2C1.SCK, U1.D1
  N3: U1.D0, S2.L2, R4.Pin_1
  N4: U1.D5, S1.L2, R3.Pin_1
  N5: U1.D6, KY-1.signal
  N6: U1.D7, KY-2.signal

notes:
  Bus i2C
  3V3  GND
  SDA  SCL

custom parts:
  NodeMCU V3.0: ESP8266 based NodeMCU
  Keyes Relay: The Keyes 5V relay module is suitable for SCM development, home appliance control. It uses a 5V~12V TIL control signal which can control DC / AC signal.
